# Fritzing sketch Gateway advanced (saved by Fritzing 0.9.3b)
circuit board: 8.46667cm x 5.64444cm

parts:
  C1 = Electrolytic Capacitor [capacitance=1µF package="100 mil [THT, electrolytic]"]
  Part2 = NRF24L01+ Breakout Board
  LED1 = smd LED [color="Red (633nm)" package="0603 [SMD]"]
  R2 = Resistor [tolerance=±5% resistance=510 package="0805 [SMD]"]
  LED3 = smd LED [color="Yellow (592nm)" package="0603 [SMD]"]
  R1 = Resistor [tolerance=±5% resistance=510 package="0805 [SMD]"]
  LED2 = smd LED [color="Green (560nm)" package="0603 [SMD]"]
  R3 = Resistor [tolerance=±5% resistance=510 package="0805 [SMD]"]
  Part1 = Arduino Nano (Rev3.0)

nets:
  GND: C1.-, Part2.GND, Part1.GND
  VCC: C1.+, Part2.VCC, Part1.3V3
  N1: Part2.CE, Part1.D9
  N2: Part2.CS, Part1.D10
  N3: Part2.SCK, Part1.D13/SCK
  N4: Part2.MOSI, Part1.D11/MOSI
  N5: Part2.MISO, Part1.D12/MISO
  N6: Part2.IRQ, Part1.D2
  N7: LED1.cathode, R2.Pin_1
  N8: LED1.anode, LED3.anode, LED2.anode
  N9: R2.Pin_0, Part1.D4
  N10: LED3.cathode, R3.Pin_1
  N11: R1.Pin_0, Part1.D5
  N12: R1.Pin_1, LED2.cathode
  N13: R3.Pin_0, Part1.D6
