# Fritzing sketch Gateway mega (saved by Fritzing 0.9.3b)
circuit board: 8.46667cm x 5.64444cm

parts:
  C1 = Electrolytic Capacitor [capacitance=470µF package="100 mil [THT, electrolytic]"]
  Part2 = NRF24L01+ Breakout Board
  Part5 = Arduino Mega 2560 (Rev3)

nets:
  GND: C1.-, Part2.GND, Part5.GND
  VCC: C1.+, Part2.VCC, Part5.3V3
  N1: Part2.CE, Part5.D40
  N2: Part2.CS, Part5.D53
  N3: Part2.SCK, Part5.D50
  N4: Part2.MOSI, Part5.D51
  N5: Part2.MISO, Part5.D52
