# Fritzing sketch Gateway normal (saved by Fritzing 0.9.3b)
circuit board: 8.46667cm x 5.64444cm

parts:
  C1 = Electrolytic Capacitor [capacitance=470µF package="100 mil [THT, electrolytic]"]
  Part2 = NRF24L01+ Breakout Board
  Part1 = Arduino Nano (Rev3.0)

nets:
  GND: C1.-, Part2.GND, Part1.GND
  VCC: C1.+, Part2.VCC, Part1.3V3
  N1: Part2.CE, Part1.D9
  N2: Part2.CS, Part1.D10
  N3: Part2.SCK, Part1.D13/SCK
  N4: Part2.MOSI, Part1.D11/MOSI
  N5: Part2.MISO, Part1.D12/MISO
  N6: Part2.IRQ, Part1.D2
