# Fritzing sketch Gateway uno ethernet (saved by Fritzing 0.9.3b)
circuit board: 8.46667cm x 5.64444cm

parts:
  C1 = Electrolytic Capacitor [capacitance=470µF package="100 mil [THT, electrolytic]"]
  Part2 = NRF24L01+ Breakout Board
  Part4 = Arduino Ethernet Shield (Rev3)

nets:
  GND: C1.-, Part2.GND, Part4.GND
  VCC: C1.+, Part2.VCC, Part4.3V3
  N1: Part2.CE, Part4.PWM_D5
  N2: Part2.CS, Part4.PWM_D6
  N3: Part2.SCK, Part4.A0
  N4: Part2.MOSI, Part4.A1
  N5: Part2.MISO, Part4.A2
