# Fritzing sketch Vento (saved by Fritzing 0.9.3b)
circuit board: 8.46667cm x 5.64444cm

parts:
  C1 = Electrolytic Capacitor [capacitance=470µF package="100 mil [THT, electrolytic]"]
  Part2 = NRF24L01+ Breakout Board
  Part1 = Arduino Nano (Rev3.0)
  U1 = 4-Channel 5v Relay Shield [package=relay-4ch5v10a]

nets:
  GND: C1.-, Part2.GND, Part1.GND, U1.GND
  VCC: C1.+, Part2.VCC, Part1.3V3
  N1: Part2.CE, Part1.D9
  N2: Part2.CS, Part1.D10
  N3: Part2.SCK, Part1.D13/SCK
  N4: Part2.MOSI, Part1.D11/MOSI
  N5: Part2.MISO, Part1.D12/MISO
  N6: Part2.IRQ, Part1.D2
  N7: Part1.D3, U1.IN1
  N8: Part1.D4, U1.IN2
  N9: Part1.D5, U1.IN3
  5V: Part1.5V, U1.VCC
  N10: U1.K1-On, U1.K2-Off, U1.K3-Off

custom parts:
  4-Channel 5v Relay Shield: 4 Channel 5v Relay Shield w. 2x SPD-06VDC-SD-C
